// Logisim project lcpu.circ as structural Verilog
module main (
);

  wire undriven;
  wire [1:0] undriven_4;
  wire [15:0] imm_q, multiplexer_1_out, ram_1_data, undriven_2, undriven_3;

  RAM #(.addrWidth(18), .dataWidth(16)) ram_1 (.data(ram_1_data));  // open: addr, sel, clk, ld, clr
  pc_16bit pc_16bit_1 ();  // open: val, op, set, clock, reset, pc, pc_1
  id_16bit id_16bit_1 (.inst(ram_1_data), .ldimm(undriven));  // open: op, regd, regi0, regi1
  Register #(.width(16)) imm (.D(ram_1_data), .en(undriven), .Q(imm_q));  // open: clk, clr
  registerFile_8x16bit registerfile_8x16bit_1 (
    .regval0(undriven_2), .regval1(undriven_3));  // open: regwrite, regread0, regread1, regval, regcanwrite, clock, reg0, reg1, reg2, reg3, reg4, reg5, reg6, reg7
  Multiplexer #(.select(2), .width(16)) multiplexer_1 (
    .in0(undriven_3), .in1(imm_q), .out(multiplexer_1_out), .sel(undriven_4));  // open: in2, in3, en
  alu_16bit alu_16bit_1 (
    .val0(undriven_2), .val1(multiplexer_1_out));  // open: cin, invert0, invert1, op, gt, eq, lt, cout, zero, result
endmodule

module registerFile_8x16bit (
  input  [15:0] reg0,
  input  [15:0] reg1,
  input  [15:0] reg2,
  input  [15:0] reg3,
  input  [15:0] reg4,
  input  [15:0] reg5,
  input  [15:0] reg6,
  input  [15:0] reg7,
  input  [2:0] regwrite,
  input  clock,
  input  [2:0] regread0,
  input  [2:0] regread1,
  input  regcanwrite,
  input  [15:0] regval,
  input  [15:0] regval0,
  input  [15:0] regval1
);

  wire demultiplexer_1_out0, demultiplexer_1_out1, demultiplexer_1_out2, demultiplexer_1_out3,
       demultiplexer_1_out4, demultiplexer_1_out5, demultiplexer_1_out6, demultiplexer_1_out7;

  Demultiplexer #(.select(3)) demultiplexer_1 (
    .out0(demultiplexer_1_out0), .out1(demultiplexer_1_out1), .out2(demultiplexer_1_out2),
    .out3(demultiplexer_1_out3), .out4(demultiplexer_1_out4), .out5(demultiplexer_1_out5),
    .out6(demultiplexer_1_out6), .out7(demultiplexer_1_out7), .in(regcanwrite), .sel(regwrite));  // open: en
  Register #(.width(16)) register_1 (.D(regval), .en(demultiplexer_1_out0), .Q(reg0), .clk(clock));  // open: clr
  Register #(.width(16)) register_2 (.D(regval), .en(demultiplexer_1_out1), .Q(reg1), .clk(clock));  // open: clr
  Register #(.width(16)) register_3 (.D(regval), .en(demultiplexer_1_out2), .Q(reg2), .clk(clock));  // open: clr
  Register #(.width(16)) register_4 (.D(regval), .en(demultiplexer_1_out3), .Q(reg3), .clk(clock));  // open: clr
  Register #(.width(16)) register_5 (.D(regval), .en(demultiplexer_1_out4), .Q(reg4), .clk(clock));  // open: clr
  Register #(.width(16)) register_6 (.D(regval), .en(demultiplexer_1_out5), .Q(reg5), .clk(clock));  // open: clr
  Register #(.width(16)) register_7 (.D(regval), .en(demultiplexer_1_out6), .Q(reg6), .clk(clock));  // open: clr
  Register #(.width(16)) register_8 (.D(regval), .en(demultiplexer_1_out7), .Q(reg7), .clk(clock));  // open: clr
  Multiplexer #(.select(3), .width(16)) multiplexer_1 (
    .in0(reg0), .in1(reg1), .in2(reg2), .in3(reg3), .in4(reg4), .in5(reg5), .in6(reg6), .in7(reg7),
    .out(regval0), .sel(regread0));  // open: en
  Multiplexer #(.select(3), .width(16)) multiplexer_2 (
    .in0(reg0), .in1(reg1), .in2(reg2), .in3(reg3), .in4(reg4), .in5(reg5), .in6(reg6), .in7(reg7),
    .out(regval1), .sel(regread1));  // open: en
  // Probe on reg0
  // Probe on reg1
  // Probe on reg2
  // Probe on reg3
  // Probe on reg4
  // Probe on reg5
  // Probe on reg6
  // Probe on reg7
endmodule

module alu_16bit (
  input  gt,
  input  eq,
  input  lt,
  input  cin,
  input  cout,
  input  zero,
  input  [15:0] val0,
  input  invert0,
  input  [3:0] op,
  input  [15:0] val1,
  input  [15:0] result,
  input  invert1
);

  wire [15:0] adder_1_out, and_1_out, bit_extender_1_out, bit_extender_2_out, bit_extender_3_out, or_1_out,
       shifter_1_out, shifter_2_out, undriven, undriven_2, xnor_1_out;

  invertmux_16bit invertmux_16bit_1 (.val(val0), .invert(invert0), .val_2(undriven));
  invertmux_16bit invertmux_16bit_2 (.val(val1), .invert(invert1), .val_2(undriven_2));
  Comparator #(.width(16)) comparator_1 (.a(undriven), .b(undriven_2), .gt(gt), .eq(eq), .lt(lt));
  Adder #(.width(16)) adder_1 (.a(undriven), .b(undriven_2), .out(adder_1_out), .cin(cin), .cout(cout));
  assign and_1_out = undriven & undriven_2;  // AND_Gate and_1, 16 bits wide
  assign or_1_out = undriven | undriven_2;  // OR_Gate or_1, 16 bits wide
  assign xnor_1_out = ~(undriven ^ undriven_2);  // XNOR_Gate xnor_1, 16 bits wide
  assign bit_extender_1_out = {{15{1'b0}}, lt};  // Bit_Extender bit_extender_1
  Shifter #(.width(16)) shifter_1 (.in(undriven), .\dist (undriven_2[3:0]), .out(shifter_1_out));
  Shifter #(.width(16), .shift("lr")) shifter_2 (.in(undriven), .\dist (undriven_2[3:0]), .out(shifter_2_out));
  assign bit_extender_2_out = {{15{1'b0}}, eq};  // Bit_Extender bit_extender_2
  assign bit_extender_3_out = {{15{1'b0}}, gt};  // Bit_Extender bit_extender_3
  Multiplexer #(.select(4), .width(16)) multiplexer_1 (
    .in0(xnor_1_out), .in1(or_1_out), .in2(and_1_out), .in3(shifter_2_out), .in4(shifter_1_out),
    .in5(adder_1_out), .in6(bit_extender_1_out), .in7(bit_extender_2_out), .in8(bit_extender_3_out),
    .out(result), .sel(op));  // open: in9, in10, in11, in12, in13, in14, in15, en
  or or_2 (zero, result[0], result[1], result[2], result[3], result[4], result[5], result[6], result[7], result[9], result[10], result[11], result[12], result[13], result[14], result[15], result[8]);
endmodule

module invertmux_16bit (
  input  [15:0] val,
  input  [15:0] val_2,
  input  invert
);

  wire [15:0] not_1_out;

  assign not_1_out = ~val;  // NOT_Gate not_1, 16 bits wide
  Multiplexer #(.width(16)) multiplexer_1 (.in0(not_1_out), .in1(val), .out(val_2), .sel(invert));  // open: en
endmodule

module pc_16bit (
  input  [15:0] pc,
  input  [1:0] op,
  input  [15:0] pc_1,
  input  [15:0] val,
  input  set,
  input  clock,
  input  reset
);

  wire [15:0] adder_1_out, adder_2_out, multiplexer_1_out;

  Adder #(.width(16)) adder_1 (.a(pc), .b(16'h1), .out(adder_1_out));  // open: cin, cout
  Adder #(.width(16)) adder_2 (.a(pc), .b(val), .out(adder_2_out));  // open: cin, cout
  Multiplexer #(.select(2), .width(16)) multiplexer_1 (
    .in0(adder_1_out), .in1(adder_2_out), .in2(val), .out(multiplexer_1_out), .sel(op));  // open: in3, en
  Register #(.width(16)) register_1 (.D(multiplexer_1_out), .en(set), .Q(pc), .clk(clock), .clr(reset));
  Adder #(.width(16)) adder_3 (.a(pc), .b(16'h1), .out(pc_1));  // open: cin, cout
endmodule

module id_16bit (
  input  ldimm,
  input  [5:0] op,
  input  [2:0] regd,
  input  [15:0] inst,
  input  [2:0] regi0,
  input  [2:0] regi1
);


  assign ldimm = inst[0];
  assign op = inst[6:1];
  assign regd = inst[9:7];
  assign regi0 = inst[12:10];
  assign regi1 = inst[15:13];
endmodule

module control (
);

  wire [7:0] rom_1_data;

  ROM rom_1 (.data(rom_1_data));  // open: addr, sel
  ROM rom_2 ();  // open: addr, data, sel
endmodule
